// Logisim project bf2.circ as structural Verilog
module ALU (
  input  [15:0] \input ,
  input  [3:0] opcode,
  output [15:0] \output 
);

  wire [15:0] adder_1_out, subtractor_1_out;

  Adder #(.width(16)) adder_1 (.a(\input ), .b(16'h1), .out(adder_1_out));  // open: cin, cout
  Subtractor #(.width(16)) subtractor_1 (.a(\input ), .b(16'h1), .out(subtractor_1_out));  // open: bin, bout
  Multiplexer #(.select(4), .width(16), .enable("false")) multiplexer_1 (
    .in1(adder_1_out), .in2(subtractor_1_out), .in3(adder_1_out), .in4(subtractor_1_out), .out(\output ),
    .sel(opcode));  // open: in0, in5, in6, in7, in8, in9, in10, in11, in12, in13, in14, in15
endmodule

module RegisterFile (
  input  [15:0] \input ,
  input  write,
  input  read,
  input  [1:0] register,
  output [15:0] \output ,
  output [15:0] PC
);

  wire demultiplexer_1_out0, demultiplexer_1_out1, demultiplexer_1_out2;
  wire [15:0] address_q, data_q;

  Demultiplexer #(.select(2), .enable("false")) demultiplexer_1 (
    .out0(demultiplexer_1_out0), .out1(demultiplexer_1_out1), .out2(demultiplexer_1_out2), .in(write),
    .sel(register));  // open: out3
  Register #(.width(16)) address (.D(\input ), .Q(address_q), .clk(demultiplexer_1_out0));  // open: en, clr
  Register #(.width(16)) data (.D(\input ), .Q(data_q), .clk(demultiplexer_1_out1));  // open: en, clr
  Register #(.width(16)) u_PC (.D(\input ), .Q(PC), .clk(demultiplexer_1_out2));  // open: en, clr
  Multiplexer #(.width(16), .enable("false")) multiplexer_1 (.in0(address_q), .in1(data_q), .out(\output ), .sel(read));
endmodule

module Decoder (
  input  [7:0] instruction,
  output [3:0] out_2
);

  ROM #(.dataWidth(4)) rom_1 (.addr(instruction), .data(out_2));  // open: sel

  // Notes on the sheet:
  //   ASCII BF commands
  //   contents of rom_1 (hex, n*v repeats v):
  //   43*0 3 6 4 5 13*0 2 0 1 28*0 7 8
  //   Internal opcode
endmodule

module DataPath (
  input  write,
  input  select,
  input  [1:0] \reg ,
  input  [3:0] opcode
);

  wire [15:0] alu_1_output, registerfile_1_output;

  RegisterFile registerfile_1 (
    .\input (alu_1_output), .write(write), .read(select), .register(\reg ), .\output (registerfile_1_output));  // open: PC
  ALU alu_1 (.\input (registerfile_1_output), .opcode(opcode), .\output (alu_1_output));
endmodule
